# Fritzing sketch nodeMCU-AP-Server (saved by Fritzing 0.9.9b)
breadboards: 1

parts:
  Grove1 = Grove Button
  Grove_LED_Red1 = Grove LED Red
  Grove2 = Grove Rotary Angle Sensor
  U1 = NodeMCU V3.0

nets:
  GND: Grove1.GND, Grove_LED_Red1.GND, Grove2.GND, U1.GND
  VCC: Grove1.VCC, Grove2.VCC, U1.3V3
  N1: Grove1.SIG, U1.D6
  N2: Grove_LED_Red1.SIG, U1.D1
  N3: Grove2.SIG, U1.A0

custom parts:
  Grove LED Red: LED red, Grove connector.
  Grove Rotary Angle Sensor: A potentiometer
  NodeMCU V3.0: NodeMcu V3 Lua WIFI Development Board
